# Fritzing sketch ArduinoPerfMeter (saved by Fritzing 0.9.2b)
breadboards: 1

parts:
  METER1 = 7-Segment Panel Voltmeter  # not connected
  Part1 = Arduino Micro (Rev3)  # not connected
  JP1 = Header 6 [package=em406]
  R1 = Resistor [tolerance=±5% resistance=220 package=THT]
  R2 = Resistor [tolerance=±5% resistance=220 package=THT]
  R3 = Resistor [tolerance=±5% resistance=220 package=THT]
  R4 = Resistor [tolerance=±5% resistance=220 package=THT]

nets:
  N1: JP1.2, R1.Pin_1
  N2: JP1.3, R2.Pin_1
  N3: JP1.4, R3.Pin_1
  N4: JP1.5, R4.Pin_1

custom parts:
  7-Segment Panel Voltmeter: 7-Segment Panel Voltmeter (4.5 - 30V)
