# Fritzing sketch ArduinoPerfMeter (saved by Fritzing 0.9.3b)
breadboards: 1

parts:
  Part1 = Arduino Micro (Rev3)
  M2 = Analog Voltmeter [package=THT]
  M1 = Analog Voltmeter [package=THT]
  M3 = Analog Voltmeter [package=THT]
  M4 = Analog Voltmeter [package=THT]

nets:
  N1: Part1.GND, M2.-, M1.-, M3.-, M4.-
  N2: Part1.D6_PWM/A7, M1.+
  N3: Part1.D9_PWM/A9, M2.+
  N4: Part1.D10_PWM/A10, M3.+
  N5: Part1.D11_PWM, M4.+

custom parts:
  Analog Voltmeter: A generic DC analog voltmeter
